# Fritzing sketch Configuring (saved by Fritzing 0.9.2b)
breadboards: 1

parts:
  Part1 = FTDI Basic Programmer
  Part2 = Arduino Uno (Rev3)
  U1 = ESP8266 WiFi Module [part_number=ESP8266]

nets:
  N1: Part1.RXI, U1.TXD
  N2: Part1.TXO, U1.RXD
  3V3: Part2.3V3, U1.VCC, U1.CH_PD
  GND: Part2.GND, U1.GPIO_0, U1.GND

custom parts:
  ESP8266 WiFi Module: Generic WiFi Module based on the ESP8266 with onboard PCB antenna and UART communications
