# Fritzing sketch ArduinoToEsp (saved by Fritzing 0.9.2b)
breadboards: 1

parts:
  U1 = ESP8266 WiFi Module [part_number=ESP8266]
  Part1 = Arduino Uno (Rev3) - ICSP
  VCC1 = Battery
  R1 = Resistor [tolerance=±5% resistance=1k package="1206 [SMD]"]
  R2 = Resistor [tolerance=±5% resistance=2.2k package="1206 [SMD]"]
  R3 = Resistor [tolerance=±5% resistance=10k package="1206 [SMD]"]
  R4 = Resistor [tolerance=±5% resistance=1k package="1206 [SMD]"]

nets:
  N1: U1.RXD, R1.Pin_1, R2.Pin_0
  N2: U1.VCC, VCC1.+, R3.Pin_0, R4.Pin_1
  N3: U1.RST, R4.Pin_0
  N4: U1.CH_PD, R3.Pin_1
  GND: U1.GND, Part1.GND, VCC1.-, R2.Pin_1
  N5: U1.TXD, Part1.D7
  N6: Part1.D8, R1.Pin_0

notes:
  5V->~3.3V Voltage Divider (1k and 2.2k)
  3.3V Power supply

custom parts:
  ESP8266 WiFi Module: Generic WiFi Module based on the ESP8266 with onboard PCB antenna and UART communications
