# Fritzing sketch v01 (saved by Fritzing 0.9.2b)
breadboards: 1

parts:
  Part1 = Arduino Uno (Rev3)
  U1 = 7-SEGMENT-4DIGIT [package=7-segment-4digit-youngsun]
  S1 = Pushbutton [package="[THT]"]
  S2 = Pushbutton [package="[THT]"]
  R1 = Resistor [tolerance=±5% resistance=220 package=THT]
  R2 = Resistor [tolerance=±5% resistance=220 package=THT]

nets:
  N1: Part1.D8, U1.16
  N2: Part1.D9_PWM, U1.8
  N3: Part1.D10_PWM/SS, U1.6
  N4: Part1.D11_PWM/MOSI, U1.3
  N5: Part1.D0/RX, S1.Pin_1, S1.Pin_2, R2.Pin_0
  N6: Part1.D1/TX, S2.Pin_1, S2.Pin_2, R1.Pin_0
  N7: Part1.D2, U1.11
  N8: Part1.D3_PWM, U1.13
  N9: Part1.D4, U1.14
  N10: Part1.D5_PWM, U1.1
  N11: Part1.D6_PWM, U1.15
  N12: Part1.5V, S1.Pin_3, S1.Pin_4, S2.Pin_3, S2.Pin_4
  N13: Part1.GND, R1.Pin_1, R2.Pin_1
