# Fritzing sketch StandaloneAtmega8Clock (saved by Fritzing 0.9.2b)
breadboards: 2

parts:
  U1 = Battery Holders [package=battery_20mm_pth_compact]
  7_Segment1 = 7 Segment Display  # not connected
  LED1 = 7-SEGMENT-4DIGIT-YOUNGSUN [package=7-segment-4digit-youngsun-longpads]
  R7 = Resistor [tolerance=±5% resistance=220 package=THT]
  R8 = Resistor [tolerance=±5% resistance=220 package=THT]
  S5 = Pushbutton [package="[THT]"]
  S6 = Pushbutton [package="[THT]"]
  IC3 = MICROCONTROLLER [package=dil28-3-simon-kit]
  C7 = Capacitor [package=cap-pth-small2]
  C8 = Electrolytic Capacitor [capacitance=1000μF package="1010 [SMD, electrolytic]"]
  R9 = Resistor [tolerance=±5% resistance=10k package=THT]
  C9 = Capacitor [package=cap-pth-small2]
  R10 = Resistor [tolerance=±5% resistance=200 package=THT]

nets:
  N1: U1.+, S5.Pin_3, S5.Pin_4, S6.Pin_3, S6.Pin_4, IC3.PD0(RXD), IC3.PD1(TXD), IC3.VCC, C8.-, R9.Pin_1, C9.1, R10.Pin_1
  N2: U1.-, R7.Pin_1, R8.Pin_1, IC3.GND, IC3.PB6(XTAL1_TOSC1), IC3.AGND, C7.1, C8.+, C9.2
  N3: LED1.DIG1, IC3.PD5(T1)
  N4: LED1.D, IC3.PB3(MOSI_OC2)
  N5: LED1.DIG3, IC3.PB2(SS_OC1B)
  N6: LED1.DIG4, IC3.PB1(OC1A)
  N7: LED1.F, IC3.PD4(XCK_T0)
  N8: LED1.COL-C, IC3.PD7(AIN1)
  N9: LED1.C, IC3.PD3(INT1)
  N10: LED1.A, IC3.PD2(INT0)
  N11: LED1.G, IC3.PD6(AIN0)
  N12: LED1.B, IC3.PB0(ICP)
  N13: R7.Pin_0, S5.Pin_1, S5.Pin_2
  N14: R8.Pin_0, S6.Pin_1, S6.Pin_2
  N15: IC3.PC6(_RESET), R9.Pin_0
  N16: IC3.AVCC, C7.2, R10.Pin_0

notes:
  2 <=> 4
  3 jest dalej 3
